# Fritzing sketch motor_config (saved by Fritzing 0.9.3b)
breadboards: 1

parts:
  L1 = Solenoid
  IC1 = H-Bridge [package=THT]
  Part1 = Arduino Uno (Rev3)
  R1 = Rotary Potentiometer (Small) [maximum_resistance=100kΩ package=THT]
  S1 = Momentary Switch [package=ksa_sealed_tac_switch]
  R2 = Resistor [tolerance=±5% resistance=10k package=THT]
  VCC1 = Battery block 9V
  C1 = Capacitor Polarized [package=cpol-radial-100uf-25v]

nets:
  N1: L1.pin1, IC1.1Y
  N2: L1.pin2, IC1.2Y
  N3: IC1.1_2EN, Part1.D9_PWM
  N4: IC1.1A, Part1.D4
  GND1: IC1.GND1, IC1.GND2, Part1.GND, R1.leg1, R2.Pin_1, VCC1.-
  N5: IC1.2A, Part1.D3_PWM
  GND3: IC1.VCC2, IC1.GND3, IC1.GND4, IC1.VCC1, S1.4, VCC1.+, C1.+, C1.-
  N6: Part1.A0, R1.leg2
  N7: Part1.D2, S1.2, R2.Pin_0
