# Fritzing sketch LCD_Arrangement (saved by Fritzing 0.9.3b)
breadboards: 1

parts:
  Part1 = Arduino Ethernet Shield (Rev3)
  U1 = LCD-16X2 [package=lcd-16x2_noholes]
  S1 = Tilt Switch [package=THT]
  R1 = Rotary Potentiometer (Small) [maximum_resistance=100kΩ package=THT]
  R2 = Resistor [tolerance=±5% resistance=220 package=THT]
  R3 = Resistor [tolerance=±5% resistance=10 package=THT]

nets:
  N1: Part1.ETH_CS, U1.E
  N2: Part1.PWM_D11, U1.R_W
  N3: Part1.SPI/D12, U1.RS
  N4: Part1.D2, U1.DB7
  N5: Part1.PWM_D3, U1.DB6
  N6: Part1.SDCS, U1.DB5
  N7: Part1.PWM_D5, U1.DB4
  N8: Part1.PWM_D6, S1.Pin_2, R3.Pin_0
  5V: Part1.5V, U1.VDD, S1.Pin_1, R1.leg1
  GND: Part1.GND, U1.VSS, U1.K, R1.leg2, R2.Pin_1, R3.Pin_1
  N9: U1.VO, R1.wiper
  N10: U1.A, R2.Pin_0
