# Fritzing sketch stepper_config(schematic) (saved by Fritzing 0.9.3b)
breadboards: 1

parts:
  UNO = Arduino Uno (Rev3)
  H_BRIDGE = H-Bridge [package=THT]
  STEPPER = Stepper Motor - Unipolar
  BATTERY = Battery block 9V

nets:
  N1: UNO.D8, H_BRIDGE.1A
  N2: UNO.D9_PWM, H_BRIDGE.2A
  N3: UNO.D10_PWM/SS, H_BRIDGE.3A
  N4: UNO.D11_PWM/MOSI, H_BRIDGE.4A
  N5: UNO.5V, H_BRIDGE.1_2EN, H_BRIDGE.3_4EN, H_BRIDGE.VCC1
  GND: UNO.GND, H_BRIDGE.GND1, H_BRIDGE.GND2, H_BRIDGE.GND3, H_BRIDGE.GND4, BATTERY.-
  N6: H_BRIDGE.1Y, STEPPER.A
  N7: H_BRIDGE.2Y, STEPPER.C
  N8: H_BRIDGE.VCC2, BATTERY.+
  N9: H_BRIDGE.3Y, STEPPER.B
  N10: H_BRIDGE.4Y, STEPPER.D
  N11: STEPPER.COMMON_1, STEPPER.COMMON_2
